# Fritzing sketch Esquematico_Transmisor_nrf24l01 (saved by Fritzing 0.9.2b)
breadboards: 1

parts:
  Parte1 = Arduino Mega ADK (Rev3)
  Componente2 = nRF24L01+
  RHT1 = Humidity and Temperature Sensor RHT03

nets:
  3V3: Parte1.3V3, Componente2.VCC
  5V: Parte1.5V, RHT1.Vcc
  GND: Parte1.GND, Componente2.GND, RHT1.GND_2
  N1: Parte1.D46, RHT1.Data-signal
  N2: Parte1.D48, Componente2.CE
  N3: Parte1.D49, Componente2.CSN
  N4: Parte1.D50/MISO, Componente2.MISO
  N5: Parte1.D51/MOSI, Componente2.MOSI
  N6: Parte1.D52/SCK, Componente2.SCK
